# Fritzing sketch esp8266_ftdi_5V (saved by Fritzing 0.9.1b)
breadboards: 1

parts:
  Espessif_Serial_Wifi_Modul_1 = ESP8266 ESP01 [part_number=ESP8266 package=THT]
  Q1 = TRANSISTOR_NPN [package=to-92-ammo]
  R1 = Resistor [tolerance=±5% resistance=22k package=THT]
  DS1 = DS18B20 1-Wire Temperature Sensor [part_number=DS18B20]
  R2 = Resistor [tolerance=±5% resistance=4.7k package=THT]
  C1 = Electrolytic Capacitor [capacitance=10µF package="100 mil [THT, electrolytic]"]
  J1 = double row male pin header, 2 pins [form="♂ (male)"]
  R3 = Resistor [tolerance=±5% resistance=6.8k package=THT]
  FTDI1 = FTDI Friend
  R4 = Resistor [tolerance=±5% resistance=10k package=THT]
  R5 = Resistor [tolerance=±5% resistance=2.2k package=THT]
  REG1 = LD33 Low-Dropout Voltage Regulator

nets:
  GND: Espessif_Serial_Wifi_Modul_1.GND, Espessif_Serial_Wifi_Modul_1.GPIO16, R1.Pin_1, DS1.GND, C1.-, J1.pin1, J1.pin2, FTDI1.GND, REG1.GND
  N1: Espessif_Serial_Wifi_Modul_1.RXD, R1.Pin_0, R4.Pin_0
  N2: Espessif_Serial_Wifi_Modul_1.TXD, Q1.E
  VCC: Espessif_Serial_Wifi_Modul_1.VCC, Espessif_Serial_Wifi_Modul_1.CH_PD, DS1.VDD, R2.Pin_1, R5.Pin_1, REG1.Vout
  N3: Espessif_Serial_Wifi_Modul_1.GPIO02, DS1.DQ, R2.Pin_0
  N4: Q1.B, R5.Pin_0
  N5: Q1.C, R3.Pin_1, FTDI1.RX
  N6: C1.+, R3.Pin_0, REG1.Vin
  N7: FTDI1.TX, R4.Pin_1

notes:
  Schaltplan ist inkonsistent, 3,3V und gnd sind verbunden!

custom parts:
  ESP8266 ESP01: Generic WiFi Module based on the ESP8266 with onboard PCB antenna and UART communications
